# Fritzing sketch dot15d4 (saved by Fritzing 1.0.1rc)
breadboards: 2

parts:
  A1 = Raspberry Pi Pico2
  nRF52840_Dongle = nRF52840 Dongle
  A2 = Raspberry Pi Pico2
  nRF52840_Dongle1 = nRF52840 Dongle

nets:
  N1: A1.pin_3, A1.pin_8, A1.pin_13, A1.pin_18, A1.pin_23, A1.pin_28, A1.pin_33, A1.pin_38, nRF52840_Dongle.GND#20, A2.pin_3, A2.pin_8, A2.pin_13, A2.pin_18, A2.pin_23, A2.pin_28, A2.pin_33, A2.pin_38, nRF52840_Dongle1.GND#20
  N2: A1.pin_4, nRF52840_Dongle.SWDCLK
  N3: A1.pin_5, nRF52840_Dongle.SWDIO
  N4: A1.pin_24, nRF52840_Dongle.0.29, nRF52840_Dongle1.0.02
  N5: A1.pin_29, nRF52840_Dongle.X1, nRF52840_Dongle1.X1
  N6: A1.pin_36, nRF52840_Dongle.OUT
  N7: A2.pin_4, nRF52840_Dongle1.SWDCLK
  N8: A2.pin_5, nRF52840_Dongle1.SWDIO
  N9: A2.pin_36, nRF52840_Dongle1.OUT

custom parts:
  Raspberry Pi Pico2: Raspberry Pi Pico 2 is our new $5 microcontroller board, built on RP2350: our new high-performance, secure microcontroller.
  nRF52840 Dongle: Nordic Semiconductor nRF52840 Dongle
